# Fritzing sketch flex-sensor-amplifier-hookup (saved by Fritzing 0.8.7b)
breadboards: 1

parts:
  R1 = Resistor [tolerance=±5% resistance=10k package=THT]
  R2 = Basic Flex Resistor
  Arduino1 = Arduino Uno (Rev3)
  R3 = Rotary Potentiometer (Small) [maximum_resistance=100kΩ package=THT]
  IC1 = IC, DIP package, 14 pins [chip_label=IC]
  C1 = Ceramic Capacitor [capacitance=100nF package="100 mil [THT, multilayer]"]

nets:
  N1: R1.Pin_0, Arduino1.5V, IC1.pin4, C1.0
  N2: R1.Pin_1, R2.pin_1, IC1.pin5
  N3: R2.Pin_2, Arduino1.GND, R3.leg2, IC1.pin11, C1.1
  N4: Arduino1.A0, R3.leg1, IC1.pin7
  N5: R3.wiper, IC1.pin6
